// Logisim project 14032098.circ as structural Verilog: 1 circuit, main circuit main
module main (
  input  z,
  input  y,
  input  x,
  input  w
);

  wire a_out, and_1_out, and_2_out, and_3_out, and_4_out, and_5_out, and_6_out, and_7_out, and_8_out,
       and_9_out, and_10_out, and_11_out, and_12_out, b_out, c_out, d_out, e_out, f_out, g_out, not_1_out,
       not_2_out, not_3_out, not_4_out;

  not not_1 (not_1_out, z);
  not not_2 (not_2_out, y);
  not not_3 (not_3_out, x);
  not not_4 (not_4_out, w);
  and and_1 (and_1_out, y, w);
  and and_2 (and_2_out, not_4_out, not_2_out);
  and and_3 (and_3_out, not_1_out, not_2_out);
  and and_4 (and_4_out, not_3_out, not_4_out);
  and and_5 (and_5_out, x, w);
  and and_6 (and_6_out, x, not_4_out);
  and and_7 (and_7_out, not_1_out, not_2_out, x);
  and and_8 (and_8_out, not_3_out, w, y);
  and and_9 (and_9_out, z, not_3_out, not_4_out);
  and and_10 (and_10_out, not_3_out, not_4_out);
  and and_11 (and_11_out, y, not_4_out);
  and and_12 (and_12_out, not_3_out, y);
  or a (a_out, and_1_out, and_2_out, x, z);
  or b (b_out, and_3_out, and_4_out, and_5_out, z);
  or c (c_out, y, w, not_3_out);
  or d (d_out, z, and_6_out, and_7_out, and_2_out, and_8_out);
  or e (e_out, and_2_out, and_9_out, and_6_out);
  or f (f_out, z, and_10_out, and_11_out, and_12_out);
  or g (g_out, and_12_out, and_7_out, and_6_out, z);
  _7_Segment_Display u_7_segment_display_1 (
    .g(g_out), .f(f_out), .a(a_out), .b(b_out), .e(e_out), .d(d_out), .c(c_out));  // open: dp
endmodule
